# Fritzing sketch rtty-arduino-beacon-si5351-sketch (saved by Fritzing 0.9.3b)

parts:
  Part1 = Arduino Uno (Rev3)
  Part2 = Adafruit Si5351A Clock Generator [part_number="Adafruit #2045"]
  ANT1 = Antenna
  U1 = mystery part, 3 pins [chip_label=Filter]

nets:
  N1: Part1.A4/SDA, Part2.SDA
  N2: Part1.A5/SCL, Part2.SCL
  3V3: Part1.3V3, Part2.VIN
  GND: Part1.GND, Part2.GND, U1.pin2
  N3: Part2.CLK0, U1.pin1
  N4: ANT1.antenna_lead, U1.pin3

custom parts:
  Adafruit Si5351A Clock Generator: Never hunt around for another crystal again, with the Si5351A clock generator breakout from Adafruit! This chip has a precision 25MHz crystal reference and internal PLL and dividers so it can generate just about any frequency, from <8KHz up to 150+ MHz. The Si5351A clock generator is an I2C controller clock generator. It uses the onboard precision clock to drive multiple PLL's and clock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
